// Logisim project flipflopD.circ as structural Verilog: 1 circuit, main circuit main
module main (
  input  in_1,
  output out_2,
  output out_3
);

  wire and_1_out, and_2_out, clock_1_out, not_1_out;

  not not_1 (not_1_out, in_1);
  Clock clock_1 (.out(clock_1_out));
  and and_1 (and_1_out, not_1_out, out_3);
  and and_2 (and_2_out, out_2, in_1);
  S_R_Flip_Flop s_r_ff_1 (
    .S(and_1_out), .clk(clock_1_out), .R(and_2_out), .Q(out_2), .Qn(out_3));  // open: preset, reset, en
endmodule
